# Fritzing sketch Wiring (saved by Fritzing 0.9.2b)
perfboards: 2

parts:
  UDN_2981_-_8-Channel_Source_Driver1 = DIP - 18 pins [package="DIP (Dual Inline) [THT]"]
  U1 = Header 1 [package=1x01_offset]
  U2 = Header 1 [package=1x01_offset]
  VCC1 = Battery block 9V
  U3 = Header 1 [package=1x01_offset]
  U4 = Header 1 [package=1x01_offset]
  Bauteil1 = Dual H-Bridge L298
  U5 = Header 1 [package=1x01_offset]
  U6 = Header 1 [package=1x01_offset]
  U7 = Header 1 [package=1x01_offset]
  U8 = Header 1 [package=1x01_offset]
  U9 = Header 1 [package=1x01_offset]
  U10 = Header 1 [package=1x01_offset]
  U11 = Header 1 [package=1x01_offset]
  U12 = Header 1 [package=1x01_offset]
  U13 = Header 1 [package=1x01_offset]
  U14 = Header 1 [package=1x01_offset]
  U15 = Header 1 [package=1x01_offset]
  U16 = Header 1 [package=1x01_offset]
  U17 = Header 1 [package=1x01_offset]
  U18 = Header 1 [package=1x01_offset]
  U19 = Header 1 [package=1x01_offset]
  U20 = Header 1 [package=1x01_offset]
  U21 = Header 1 [package=1x01_offset]
  U22 = Header 1 [package=1x01_offset]
  U23 = Header 1 [package=1x01_offset]
  J1 = Basic Servo
  U24 = Header 1 [package=1x01_offset]
  U25 = Header 1 [package=1x01_offset]
  U26 = Header 1 [package=1x01_offset]
  U27 = Header 1 [package=1x01_offset]
  U28 = Header 1 [package=1x01_offset]
  U29 = Header 1 [package=1x01_offset]
  U30 = Header 1 [package=1x01_offset]
  U31 = Header 1 [package=1x01_offset]
  U32 = Header 1 [package=1x01_offset]
  U33 = Header 1 [package=1x01_offset]
  U34 = Header 1 [package=1x01_offset]
  U35 = Header 1 [package=1x01_offset]
  M1 = DC Motor
  U36 = Header 1 [package=1x01_offset]
  U37 = Header 1 [package=1x01_offset]
  U38 = Header 1 [package=1x01_offset]
  U39 = Header 1 [package=1x01_offset]
  U40 = Header 1 [package=1x01_offset]
  U41 = Header 1 [package=1x01_offset]
  U42 = Header 1 [package=1x01_offset]
  U43 = Header 1 [package=1x01_offset]
  R12 = Resistor [tolerance=±5% resistance=1k package="1206 [SMD]"]
  R14 = Resistor [tolerance=±5% resistance=1k package="1206 [SMD]"]
  R16 = Resistor [tolerance=±5% resistance=1k package="1206 [SMD]"]
  R17 = Resistor [tolerance=±5% resistance=1k package="1206 [SMD]"]
  R18 = Resistor [tolerance=±5% resistance=1k package="1206 [SMD]"]
  R19 = Resistor [tolerance=±5% resistance=1k package="1206 [SMD]"]
  R20 = Resistor [tolerance=±5% resistance=1k package="1206 [SMD]"]
  R21 = Resistor [tolerance=±5% resistance=1k package="1206 [SMD]"]
  R22 = Resistor [tolerance=±5% resistance=1k package="1206 [SMD]"]
  R23 = Resistor [tolerance=±5% resistance=1k package="1206 [SMD]"]
  R24 = Resistor [tolerance=±5% resistance=1k package="1206 [SMD]"]
  PART1 = SparkFun Block for Intel Edison - GPIO [part_number=DEV-13038]
  Bauteil2 = Dual H-Bridge L298
  M2 = DC Motor
  J2 = Basic Servo
  VCC2 = Battery block 9V
  JP1 = M10X2 [package=2x10_lock]
  JP2 = M10X2 [package=2x10_lock]
  U44 = Header 1 [package=1x01_offset]
  U45 = Header 1 [package=1x01_offset]
  U46 = Header 1 [package=1x01_offset]
  U47 = Header 1 [package=1x01_offset]
  U48 = Header 1 [package=1x01_offset]
  UDN_2981_-_8-Channel_Source_Driver2 = DIP - 18 pins [package="DIP (Dual Inline) [THT]"]
  U49 = Header 1 [package=1x01_offset]
  U50 = Header 1 [package=1x01_offset]
  U51 = Header 1 [package=1x01_offset]
  Raspberry_Pi1 = Raspberry Pi 2
  U52 = Header 1 [package=1x01_offset]
  U53 = Header 1 [package=1x01_offset]
  U54 = Header 1 [package=1x01_offset]
  U55 = Header 1 [package=1x01_offset]
  U56 = Header 1 [package=1x01_offset]
  U57 = Header 1 [package=1x01_offset]
  U58 = Header 1 [package=1x01_offset]  # not connected
  U59 = Header 1 [package=1x01_offset]
  U60 = Header 1 [package=1x01_offset]
  U61 = Header 1 [package=1x01_offset]  # not connected
  U62 = Header 1 [package=1x01_offset]
  U63 = Header 1 [package=1x01_offset]  # not connected
  U64 = Header 1 [package=1x01_offset]
  U65 = Header 1 [package=1x01_offset]
  U66 = Header 1 [package=1x01_offset]
  U67 = Header 1 [package=1x01_offset]
  U68 = Header 1 [package=1x01_offset]
  U69 = Header 1 [package=1x01_offset]
  U70 = Header 1 [package=1x01_offset]
  U71 = Header 1 [package=1x01_offset]
  U72 = Header 1 [package=1x01_offset]
  U73 = Header 1 [package=1x01_offset]  # not connected
  U76 = Header 1 [package=1x01_offset]
  U77 = mystery part, 4 pins [chip_label=R]
  U78 = mystery part, 4 pins [chip_label=R]
  U79 = mystery part, 4 pins [chip_label=R]
  U80 = mystery part, 4 pins [chip_label=R]
  U81 = mystery part, 4 pins [chip_label=R]
  U82 = mystery part, 4 pins [chip_label=R]

nets:
  N1: UDN_2981_-_8-Channel_Source_Driver1.In_1, U27.1, PART1.GP13
  N2: UDN_2981_-_8-Channel_Source_Driver1.In_2, U26.1, PART1.GP44
  N3: UDN_2981_-_8-Channel_Source_Driver1.In_3, U25.1, PART1.GP45
  N4: UDN_2981_-_8-Channel_Source_Driver1.In_4, U32.1
  N5: UDN_2981_-_8-Channel_Source_Driver1.In_5, U24.1
  N6: UDN_2981_-_8-Channel_Source_Driver1.In_6, U33.1, PART1.GP46
  N7: UDN_2981_-_8-Channel_Source_Driver1.In_7, U31.1, PART1.GP47
  N8: UDN_2981_-_8-Channel_Source_Driver1.In_8, U34.1, PART1.GP48
  VCC: UDN_2981_-_8-Channel_Source_Driver1.Vcc, Bauteil1.5V, Bauteil1.+5V, U5.1, U22.1, J1.vcc
  GND: UDN_2981_-_8-Channel_Source_Driver1.GND, U2.1, VCC1.-, U4.1, Bauteil1.GND, U9.1, U10.1, U11.1, U12.1, U13.1, U14.1, U15.1, U16.1, U18.1, U21.1, J1.gnd, U35.1
  N9: UDN_2981_-_8-Channel_Source_Driver1.Out_8, R23.Pin_0
  N10: UDN_2981_-_8-Channel_Source_Driver1.Out_7, R22.Pin_0
  N11: UDN_2981_-_8-Channel_Source_Driver1.Out_6, R21.Pin_0
  N12: UDN_2981_-_8-Channel_Source_Driver1.Out_5, R19.Pin_0, R20.Pin_0
  N13: UDN_2981_-_8-Channel_Source_Driver1.Out_4, R17.Pin_0, R18.Pin_0
  N14: UDN_2981_-_8-Channel_Source_Driver1.Out_3, R16.Pin_0, R24.Pin_0
  N15: UDN_2981_-_8-Channel_Source_Driver1.Out_2, R12.Pin_0
  N16: UDN_2981_-_8-Channel_Source_Driver1.Out_1, U23.1, J1.pulse
  N17: U1.1, VCC1.+, U3.1, Bauteil1.VMS
  N18: Bauteil1.MOTORA1, M1.pin_1
  N19: Bauteil1.MOTORA2, M1.pin_2
  N20: Bauteil1.ENA, U6.1, U30.1, PART1.GP14
  N21: Bauteil1.IN1, U7.1, U29.1, PART1.GP12
  N22: Bauteil1.IN2, U8.1, U28.1, PART1.GP15
  N23: U17.1, R21.Pin_1
  N24: U19.1, R22.Pin_1
  N25: U20.1, R23.Pin_1
  N26: U36.1, R20.Pin_1
  N27: U37.1, R19.Pin_1
  N28: U38.1, R18.Pin_1
  N29: U39.1, R17.Pin_1
  N30: U40.1, R16.Pin_1
  N31: U41.1, R24.Pin_1
  N32: U42.1, R14.Pin_1
  N33: U43.1, R12.Pin_1
  N34: Bauteil2.MOTORA1, M2.pin_1
  N35: Bauteil2.MOTORA2, M2.pin_2
  N36: Bauteil2.VMS, VCC2.+, U46.1, U47.1
  GND_2: Bauteil2.GND, J2.gnd, VCC2.-, JP2.2, U45.1, U48.1, UDN_2981_-_8-Channel_Source_Driver2.GND, Raspberry_Pi1.GND, U54.1, U55.1, U57.1, U59.1, U64.1, U67.1, U68.1, U70.1, U78.pin4
  VCC_2: Bauteil2.5V, Bauteil2.+5V, J2.vcc, U44.1, UDN_2981_-_8-Channel_Source_Driver2.Vcc, U53.1
  N37: Bauteil2.ENA, JP2.10, U51.1, Raspberry_Pi1.GPIO6
  N38: Bauteil2.IN1, JP2.8, U50.1, Raspberry_Pi1.GPIO13
  N39: Bauteil2.IN2, JP2.12, U49.1, Raspberry_Pi1.GPIO5
  N40: J2.pulse, UDN_2981_-_8-Channel_Source_Driver2.Out_8, U52.1
  N41: JP1.9, UDN_2981_-_8-Channel_Source_Driver2.In_8, Raspberry_Pi1.GPIO18
  N42: JP2.1, UDN_2981_-_8-Channel_Source_Driver2.In_1, Raspberry_Pi1.GPIO21
  N43: JP2.3, UDN_2981_-_8-Channel_Source_Driver2.In_2, Raspberry_Pi1.GPIO20
  N44: JP2.4, UDN_2981_-_8-Channel_Source_Driver2.In_6, Raspberry_Pi1.GPIO26
  N45: JP2.5, UDN_2981_-_8-Channel_Source_Driver2.In_3, Raspberry_Pi1.GPIO16
  N46: JP2.6, UDN_2981_-_8-Channel_Source_Driver2.In_7, Raspberry_Pi1.GPIO19
  N47: JP2.18, UDN_2981_-_8-Channel_Source_Driver2.In_4, Raspberry_Pi1.GPIO11
  N48: JP2.20, UDN_2981_-_8-Channel_Source_Driver2.In_5, Raspberry_Pi1.GPIO9
  N49: UDN_2981_-_8-Channel_Source_Driver2.Out_7, U79.pin1, U79.pin2
  N50: UDN_2981_-_8-Channel_Source_Driver2.Out_6, U80.pin1, U80.pin2
  N51: UDN_2981_-_8-Channel_Source_Driver2.Out_5, U81.pin1, U81.pin2
  N52: UDN_2981_-_8-Channel_Source_Driver2.Out_4, U82.pin1, U82.pin2
  N53: UDN_2981_-_8-Channel_Source_Driver2.Out_3, U78.pin2
  N54: UDN_2981_-_8-Channel_Source_Driver2.Out_2, U77.pin2
  N55: UDN_2981_-_8-Channel_Source_Driver2.Out_1, U77.pin1
  N56: U56.1, U79.pin3
  N57: U60.1, U80.pin3
  N58: U62.1, U80.pin4
  N59: U65.1, U81.pin3
  N60: U66.1, U81.pin4
  N61: U69.1, U78.pin3
  N62: U71.1, U77.pin3
  N63: U72.1, U77.pin4
  N64: U76.1, U82.pin4

custom parts:
  DIP - 18 pins: Recommended for high-side switching applications that benefit from separate logic and load grounds, these devices encompass load supply voltages to 50 V and output currents to -500 mA. These 8-channel source drivers are useful for interfacing between low-level logic and high-current loads. Typical loads include relays, solenoids, lamps, stepper and/or servo motors, print hammers, and LEDs.
  Dual H-Bridge L298: Description:The L298N driver module, using ST's L298N chip can directly drive two 3-30V DC motor, and provides a 5V output interface can 5V single-chip circuitry to supply, support 3.3VMCU control, you can easily control the DC motor speed and direction, you can also control the 2-phase stepper motor, smart car essential. Features: Driver: L298N Dual H Bridge DC Motor Driver IC Driven part of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
  SparkFun Block for Intel Edison - GPIO: The Intel® Edison is an ultra small computing platform that will change the way you look at embedded electronics. Each Edison is packed with a huge amount of tech goodies into a tiny package while still providing the same robust strength of your go-to single board computer. Powered by the Intel® Atom™ SoC dual-core CPU and including an integrated WiFi, Bluetooth LE, and a 70-pin connector to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
