# Fritzing sketch ControlBoard (saved by Fritzing 0.9.2b)
perfboards: 1

parts:
  J1 = female pin header, 12 pins [form="♀ (female)"]  # not connected
  J2 = female pin header, 12 pins [form="♀ (female)"]
  J3 = female pin header, 6 pins [form="♀ (female)"]
  J4 = female pin header, 6 pins [form="♀ (female)"]  # not connected
  Redbear_DUO = IC, DIP package, 24 pins [chip_label="Redbear DUO"]  # not connected
  J5 = female pin header, 4 pins [form="♀ (female)"]  # not connected
  BLE_Nano = IC, DIP package, 12 pins [chip_label="BLE Nano"]  # not connected

nets:
  N1: J2.pin2, J3.pin2
